// Logisim project stack_logisim_normal.circ as structural Verilog: 16 circuits, main circuit main
module main (
  input  CLK,
  input  RESET,
  input  [1:0] COMMAND,
  input  [2:0] INDEX,
  input  [3:0] IO_DATA_in,
  output [3:0] IO_DATA_out
);

  stack stack_1 (
    .CLK(CLK), .RESET(RESET), .COMMAND(COMMAND), .INDEX(INDEX), .IO_DATA_in(IO_DATA_in),
    .IO_DATA_out(IO_DATA_out));
endmodule

module stack (
  input  CLK,
  input  RESET,
  input  [1:0] COMMAND,
  input  [2:0] INDEX,
  input  [3:0] IO_DATA_in,
  output [3:0] IO_DATA_out
);

  wire not_1_out, transmission_1_p2;
  wire [2:0] count_1_indm5;
  wire [3:0] transmission_1_p3;

  not not_1 (not_1_out, transmission_1_p2);
  // Transmission_Gate #(.width(4)) transmission_1: pin names not known; wires that end beside it: not_1_out, transmission_1_p2, transmission_1_p3
  and and_1 (transmission_1_p2, COMMAND[1], CLK);
  COUNT count_1 (.COMMAND(COMMAND), .CLK(CLK), .RESET(RESET), .INDEX(INDEX), .INDm5(count_1_indm5));
  MEM5x4 mem5x4_1 (
    .INDEX(count_1_indm5), .IDATA(IO_DATA_in), .RESET(RESET), .COMMAND(COMMAND), .CLK(CLK),
    .ODATA(transmission_1_p3));

  assign IO_DATA_out = IO_DATA_in;

  // Notes on the sheet:
  //   your circuit must be here
endmodule

module COUNT (
  input  [1:0] COMMAND,
  input  CLK,
  input  RESET,
  input  [2:0] INDEX,
  output [2:0] INDm5
);

  wire and_1_out, and_2_out;
  wire [2:0] get_shift_1_shift, pointer_1_ind;

  and and_1 (and_1_out, COMMAND[0], CLK, ~COMMAND[1]);  // AND_Gate
  and and_2 (and_2_out, ~COMMAND[0], CLK, COMMAND[1]);  // AND_Gate
  POINTER pointer_1 (.UP(and_1_out), .DOWN(and_2_out), .RESET(RESET), .IND(pointer_1_ind));
  GET_SHIFT get_shift_1 (.COMMAND(COMMAND), .INDEX(INDEX), .SHIFT(get_shift_1_shift));
  CALC_IND calc_ind_1 (.IND(pointer_1_ind), .SHIFT(get_shift_1_shift), .INDm5(INDm5));
endmodule

module POINTER (
  input  UP,
  input  DOWN,
  input  RESET,
  output [2:0] IND
);

  wire and_1_out, and_2_out, and_3_out, and_4_out, and_5_out, and_6_out, LEDGE, or_1_out, or_2_out, or_3_out,
       REDGE, ttriger_1_nq, ttriger_2_nq, xor_1_out, xor_2_out, xor_3_out, xor_4_out;

  or or_1 (or_1_out, UP, DOWN);
  xor xor_1 (xor_1_out, UP, DOWN);
  and and_1 (and_1_out, UP, REDGE);
  and and_2 (and_2_out, DOWN, LEDGE);
  ExactlyOne xor_2 (.out(xor_2_out), .in0(IND[0]), .in1(and_2_out), .in2(and_1_out), .in3(or_1_out));
  and and_3 (and_3_out, UP, IND[0]);
  TTRIGER ttriger_1 (.D(xor_2_out), .C(xor_1_out), .R(RESET), .Q(IND[0]), .nQ(ttriger_1_nq));
  and and_4 (and_4_out, DOWN, ttriger_1_nq);
  or or_2 (or_2_out, and_3_out, and_4_out);
  ExactlyOne xor_3 (.out(xor_3_out), .in0(IND[1]), .in1(and_2_out), .in2(or_2_out));
  TTRIGER ttriger_2 (.D(xor_3_out), .C(xor_1_out), .R(RESET), .Q(IND[1]), .nQ(ttriger_2_nq));
  and and_5 (and_5_out, and_3_out, IND[1]);
  and and_6 (and_6_out, and_4_out, ttriger_2_nq);
  or or_3 (or_3_out, and_5_out, and_6_out);
  ExactlyOne xor_4 (.out(xor_4_out), .in0(IND[2]), .in1(and_1_out), .in2(or_3_out));
  TTRIGER ttriger_3 (.D(xor_4_out), .C(xor_1_out), .R(RESET), .Q(IND[2]));  // open: nQ
  and and_7 (REDGE, ~IND[0], ~IND[1], IND[2]);  // AND_Gate
  and and_8 (LEDGE, ~IND[0], ~IND[1], ~IND[2]);  // AND_Gate
endmodule

module GET_SHIFT (
  input  [1:0] COMMAND,
  input  [2:0] INDEX,
  output [2:0] SHIFT
);

  wire and_1_out, and_2_out, and_3_out, and_4_out, not_1_out, not_2_out, not_3_out, not_4_out, not_5_out,
       not_6_out, not_7_out, not_8_out, not_9_out;
  wire [2:0] and_5_out, and_8_out, and_11_out, and_14_out;

  not not_1 (not_1_out, COMMAND[0]);
  not not_2 (not_2_out, COMMAND[1]);
  not not_3 (not_3_out, COMMAND[1]);
  not not_4 (not_4_out, COMMAND[0]);
  not not_5 (not_5_out, and_1_out);
  not not_6 (not_6_out, and_1_out);
  and and_1 (and_1_out, not_1_out, not_2_out);
  not not_7 (not_7_out, and_2_out);
  not not_8 (not_8_out, and_2_out);
  and and_2 (and_2_out, COMMAND[0], not_3_out);
  not not_9 (not_9_out, and_3_out);
  and and_3 (and_3_out, not_4_out, COMMAND[1]);
  and and_4 (and_4_out, COMMAND[0], COMMAND[1]);
  and and_5 (and_5_out[0], not_5_out, and_1_out);
  and and_6 (and_5_out[1], not_6_out, and_1_out);
  and and_7 (and_5_out[2], and_1_out, and_1_out);
  and and_8 (and_8_out[0], not_7_out, and_2_out);
  and and_9 (and_8_out[1], not_8_out, and_2_out);
  and and_10 (and_8_out[2], and_2_out, and_2_out);
  and and_11 (and_11_out[0], and_3_out, and_3_out);
  and and_12 (and_11_out[1], not_9_out, and_3_out);
  and and_13 (and_11_out[2], and_3_out, and_3_out);
  and and_14 (and_14_out[0], INDEX[0], and_4_out);
  and and_15 (and_14_out[1], INDEX[1], and_4_out);
  and and_16 (and_14_out[2], INDEX[2], and_4_out);
  assign SHIFT = and_5_out | and_8_out | and_11_out | and_14_out;  // OR_Gate or_1, 3 bits wide
endmodule

module CALC_IND (
  input  [2:0] IND,
  input  [2:0] SHIFT,
  output [2:0] INDm5
);

  wire [3:0] dif4_1_d, not_1_out, sum4_1_s;

  not not_1 (not_1_out[0], 1'b0);
  not not_2 (not_1_out[3], 1'b0);
  SUM4 sum4_1 (.A1({not_1_out[3], 2'b00, not_1_out[0]}), .A2({1'b0, IND}), .S(sum4_1_s));
  DIF4 dif4_1 (.A1(sum4_1_s), .A2({1'b0, SHIFT}), .D(dif4_1_d));
  MOD5 mod5_1 (.A(dif4_1_d), .Am5(INDm5));
endmodule

module SUM4 (
  input  [3:0] A1,
  input  [3:0] A2,
  output [3:0] S
);

  wire sum_1_cout, sum_2_cout, sum_3_cout;

  SUM sum_1 (.Cin(1'b0), .A1(A1[0]), .A2(A2[0]), .S(S[0]), .Cout(sum_1_cout));
  SUM sum_2 (.Cin(sum_1_cout), .A1(A1[1]), .A2(A2[1]), .S(S[1]), .Cout(sum_2_cout));
  SUM sum_3 (.Cin(sum_2_cout), .A1(A1[2]), .A2(A2[2]), .S(S[2]), .Cout(sum_3_cout));
  SUM sum_4 (.Cin(sum_3_cout), .A1(A1[3]), .A2(A2[3]), .S(S[3]));  // open: Cout
endmodule

module SUM (
  input  Cin,
  input  A1,
  input  A2,
  output S,
  output Cout
);

  wire or_1_out, or_2_out, or_3_out;

  or or_1 (or_1_out, Cin, A1);
  or or_2 (or_2_out, Cin, A2);
  or or_3 (or_3_out, A1, A2);
  ExactlyOne xor_1 (.out(S), .in0(Cin), .in1(A1), .in2(A2));
  and and_1 (Cout, or_1_out, or_2_out, or_3_out);
endmodule

module DIF4 (
  input  [3:0] A1,
  input  [3:0] A2,
  output [3:0] D
);

  wire dif_1_bout, dif_2_bout, dif_3_bout;

  DIF dif_1 (.Bin(1'b0), .A1(A1[0]), .A2(A2[0]), .D(D[0]), .Bout(dif_1_bout));
  DIF dif_2 (.Bin(dif_1_bout), .A1(A1[1]), .A2(A2[1]), .D(D[1]), .Bout(dif_2_bout));
  DIF dif_3 (.Bin(dif_2_bout), .A1(A1[2]), .A2(A2[2]), .D(D[2]), .Bout(dif_3_bout));
  DIF dif_4 (.Bin(dif_3_bout), .A1(A1[3]), .A2(A2[3]), .D(D[3]));  // open: Bout
endmodule

module DIF (
  input  Bin,
  input  A1,
  input  A2,
  output D,
  output Bout
);

  wire and_1_out, and_2_out, not_1_out, not_2_out, xor_2_out;

  xor xor_1 (D, Bin, A1, A2);
  xor xor_2 (xor_2_out, A1, A2);
  and and_1 (and_1_out, Bin, not_1_out);
  not not_1 (not_1_out, xor_2_out);
  or or_1 (Bout, and_1_out, and_2_out);
  not not_2 (not_2_out, A1);
  and and_2 (and_2_out, not_2_out, A2);
endmodule

module MOD5 (
  input  [3:0] A,
  output [2:0] Am5
);

  wire and_1_out, and_2_out, and_3_out, and_4_out, and_5_out, and_6_out, and_7_out, and_8_out, and_9_out,
       and_10_out, and_11_out, and_12_out, and_13_out, and_14_out, and_15_out, and_16_out, not_1_out,
       not_2_out, not_3_out, not_4_out, not_5_out, not_6_out, not_7_out, not_8_out, not_9_out, not_10_out,
       not_11_out, not_12_out, not_13_out, not_14_out, not_15_out, not_16_out, not_17_out, not_18_out,
       not_19_out, not_20_out, not_21_out, not_22_out, not_23_out, not_24_out, not_25_out, not_26_out,
       not_27_out, not_28_out, not_29_out, not_30_out, not_31_out, not_32_out, not_33_out, not_34_out,
       not_35_out, not_36_out, not_37_out, not_38_out, not_39_out, not_40_out, not_41_out, not_42_out,
       not_43_out, not_44_out, not_45_out, not_46_out, not_47_out, not_48_out, not_49_out, not_50_out,
       not_51_out, not_52_out, not_53_out, not_54_out, not_55_out, not_56_out, not_57_out, not_58_out,
       not_59_out, not_60_out, not_61_out, not_62_out, not_63_out, not_64_out;
  wire [2:0] and_17_out, and_20_out, and_23_out, and_26_out, and_29_out, and_32_out, and_35_out, and_38_out,
       and_41_out, and_44_out, and_47_out, and_50_out, and_53_out, and_56_out, and_59_out, and_62_out;

  not not_1 (not_1_out, A[0]);
  not not_2 (not_2_out, A[1]);
  not not_3 (not_3_out, A[2]);
  not not_4 (not_4_out, A[3]);
  not not_5 (not_5_out, A[1]);
  not not_6 (not_6_out, A[2]);
  not not_7 (not_7_out, A[3]);
  not not_8 (not_8_out, A[0]);
  not not_9 (not_9_out, A[2]);
  not not_10 (not_10_out, A[3]);
  not not_11 (not_11_out, A[2]);
  not not_12 (not_12_out, A[3]);
  not not_13 (not_13_out, A[0]);
  not not_14 (not_14_out, A[1]);
  not not_15 (not_15_out, A[3]);
  not not_16 (not_16_out, A[1]);
  not not_17 (not_17_out, A[3]);
  not not_18 (not_18_out, A[0]);
  not not_19 (not_19_out, A[3]);
  not not_20 (not_20_out, A[3]);
  not not_21 (not_21_out, A[0]);
  not not_22 (not_22_out, A[1]);
  not not_23 (not_23_out, A[2]);
  not not_24 (not_24_out, A[1]);
  not not_25 (not_25_out, A[2]);
  not not_26 (not_26_out, A[0]);
  not not_27 (not_27_out, A[2]);
  not not_28 (not_28_out, A[2]);
  not not_29 (not_29_out, A[0]);
  not not_30 (not_30_out, A[1]);
  not not_31 (not_31_out, A[1]);
  not not_32 (not_32_out, A[0]);
  and and_1 (and_1_out, not_1_out, not_2_out, not_3_out, not_4_out);
  and and_2 (and_2_out, A[0], not_5_out, not_6_out, not_7_out);
  and and_3 (and_3_out, not_8_out, A[1], not_9_out, not_10_out);
  and and_4 (and_4_out, A[0], A[1], not_11_out, not_12_out);
  and and_5 (and_5_out, not_13_out, not_14_out, A[2], not_15_out);
  and and_6 (and_6_out, A[0], not_16_out, A[2], not_17_out);
  and and_7 (and_7_out, not_18_out, A[1], A[2], not_19_out);
  and and_8 (and_8_out, A[0], A[1], A[2], not_20_out);
  and and_9 (and_9_out, not_21_out, not_22_out, not_23_out, A[3]);
  and and_10 (and_10_out, A[0], not_24_out, not_25_out, A[3]);
  and and_11 (and_11_out, not_26_out, A[1], not_27_out, A[3]);
  and and_12 (and_12_out, A[0], A[1], not_28_out, A[3]);
  and and_13 (and_13_out, not_29_out, not_30_out, A[2], A[3]);
  and and_14 (and_14_out, A[0], not_31_out, A[2], A[3]);
  and and_15 (and_15_out, not_32_out, A[1], A[2], A[3]);
  and and_16 (and_16_out, A[0], A[1], A[2], A[3]);
  not not_33 (not_33_out, and_1_out);
  and and_17 (and_17_out[0], not_33_out, and_1_out);
  not not_34 (not_34_out, and_1_out);
  and and_18 (and_17_out[1], not_34_out, and_1_out);
  not not_35 (not_35_out, and_1_out);
  and and_19 (and_17_out[2], not_35_out, and_1_out);
  and and_20 (and_20_out[0], and_2_out, and_2_out);
  not not_36 (not_36_out, and_2_out);
  and and_21 (and_20_out[1], not_36_out, and_2_out);
  not not_37 (not_37_out, and_2_out);
  and and_22 (and_20_out[2], not_37_out, and_2_out);
  not not_38 (not_38_out, and_3_out);
  and and_23 (and_23_out[0], not_38_out, and_3_out);
  and and_24 (and_23_out[1], and_3_out, and_3_out);
  not not_39 (not_39_out, and_3_out);
  and and_25 (and_23_out[2], not_39_out, and_3_out);
  and and_26 (and_26_out[0], and_4_out, and_4_out);
  and and_27 (and_26_out[1], and_4_out, and_4_out);
  not not_40 (not_40_out, and_4_out);
  and and_28 (and_26_out[2], not_40_out, and_4_out);
  not not_41 (not_41_out, and_5_out);
  and and_29 (and_29_out[0], not_41_out, and_5_out);
  not not_42 (not_42_out, and_5_out);
  and and_30 (and_29_out[1], not_42_out, and_5_out);
  and and_31 (and_29_out[2], and_5_out, and_5_out);
  not not_43 (not_43_out, and_6_out);
  and and_32 (and_32_out[0], not_43_out, and_6_out);
  not not_44 (not_44_out, and_6_out);
  and and_33 (and_32_out[1], not_44_out, and_6_out);
  not not_45 (not_45_out, and_6_out);
  and and_34 (and_32_out[2], not_45_out, and_6_out);
  and and_35 (and_35_out[0], and_7_out, and_7_out);
  not not_46 (not_46_out, and_7_out);
  and and_36 (and_35_out[1], not_46_out, and_7_out);
  not not_47 (not_47_out, and_7_out);
  and and_37 (and_35_out[2], not_47_out, and_7_out);
  not not_48 (not_48_out, and_8_out);
  and and_38 (and_38_out[0], not_48_out, and_8_out);
  and and_39 (and_38_out[1], and_8_out, and_8_out);
  not not_49 (not_49_out, and_8_out);
  and and_40 (and_38_out[2], not_49_out, and_8_out);
  and and_41 (and_41_out[0], and_9_out, and_9_out);
  and and_42 (and_41_out[1], and_9_out, and_9_out);
  not not_50 (not_50_out, and_9_out);
  and and_43 (and_41_out[2], not_50_out, and_9_out);
  not not_51 (not_51_out, and_10_out);
  and and_44 (and_44_out[0], not_51_out, and_10_out);
  not not_52 (not_52_out, and_10_out);
  and and_45 (and_44_out[1], not_52_out, and_10_out);
  and and_46 (and_44_out[2], and_10_out, and_10_out);
  not not_53 (not_53_out, and_11_out);
  and and_47 (and_47_out[0], not_53_out, and_11_out);
  not not_54 (not_54_out, and_11_out);
  and and_48 (and_47_out[1], not_54_out, and_11_out);
  not not_55 (not_55_out, and_11_out);
  and and_49 (and_47_out[2], not_55_out, and_11_out);
  and and_50 (and_50_out[0], and_12_out, and_12_out);
  not not_56 (not_56_out, and_12_out);
  and and_51 (and_50_out[1], not_56_out, and_12_out);
  not not_57 (not_57_out, and_12_out);
  and and_52 (and_50_out[2], not_57_out, and_12_out);
  not not_58 (not_58_out, and_13_out);
  and and_53 (and_53_out[0], not_58_out, and_13_out);
  and and_54 (and_53_out[1], and_13_out, and_13_out);
  not not_59 (not_59_out, and_13_out);
  and and_55 (and_53_out[2], not_59_out, and_13_out);
  and and_56 (and_56_out[0], and_14_out, and_14_out);
  and and_57 (and_56_out[1], and_14_out, and_14_out);
  not not_60 (not_60_out, and_14_out);
  and and_58 (and_56_out[2], not_60_out, and_14_out);
  not not_61 (not_61_out, and_15_out);
  and and_59 (and_59_out[0], not_61_out, and_15_out);
  not not_62 (not_62_out, and_15_out);
  and and_60 (and_59_out[1], not_62_out, and_15_out);
  and and_61 (and_59_out[2], and_15_out, and_15_out);
  not not_63 (not_63_out, and_16_out);
  and and_62 (and_62_out[0], not_63_out, and_16_out);
  not not_64 (not_64_out, and_16_out);
  and and_63 (and_62_out[1], not_64_out, and_16_out);
  and and_64 (and_62_out[2], and_16_out, and_16_out);
  assign Am5 = and_17_out | and_20_out | and_23_out | and_26_out | and_29_out | and_32_out | and_35_out | and_38_out | and_41_out | and_44_out | and_47_out | and_50_out | and_53_out | and_56_out | and_59_out | and_62_out;  // OR_Gate or_1, 3 bits wide
endmodule

module MEM5x4 (
  input  [2:0] INDEX,
  input  [3:0] IDATA,
  input  RESET,
  input  [1:0] COMMAND,
  input  CLK,
  output [3:0] ODATA
);

  wire and_1_out, and_2_out, and_3_out, and_4_out, and_5_out, and_6_out, not_1_out, three_to_five_1_m0,
       three_to_five_1_m1, three_to_five_1_m2, three_to_five_1_m3, three_to_five_1_m4;
  wire [3:0] mem4_1_odata, mem4_2_odata, mem4_3_odata, mem4_4_odata, mem4_5_odata;

  not not_1 (not_1_out, COMMAND[1]);
  THREE_TO_FIVE three_to_five_1 (
    .INDEX(INDEX), .M0(three_to_five_1_m0), .M1(three_to_five_1_m1), .M2(three_to_five_1_m2),
    .M3(three_to_five_1_m3), .M4(three_to_five_1_m4));
  and and_1 (and_1_out, COMMAND[0], not_1_out);
  and and_2 (and_2_out, three_to_five_1_m0, CLK);
  and and_3 (and_3_out, three_to_five_1_m1, CLK);
  and and_4 (and_4_out, three_to_five_1_m2, CLK);
  and and_5 (and_5_out, three_to_five_1_m3, CLK);
  and and_6 (and_6_out, three_to_five_1_m4, CLK);
  MEM4 mem4_1 (.IDATA(IDATA), .RESET(RESET), .W(and_1_out), .CLK(and_2_out), .ODATA(mem4_1_odata));
  MEM4 mem4_2 (.IDATA(IDATA), .RESET(RESET), .W(and_1_out), .CLK(and_3_out), .ODATA(mem4_2_odata));
  MEM4 mem4_3 (.IDATA(IDATA), .RESET(RESET), .W(and_1_out), .CLK(and_4_out), .ODATA(mem4_3_odata));
  MEM4 mem4_4 (.IDATA(IDATA), .RESET(RESET), .W(and_1_out), .CLK(and_5_out), .ODATA(mem4_4_odata));
  MEM4 mem4_5 (.IDATA(IDATA), .RESET(RESET), .W(and_1_out), .CLK(and_6_out), .ODATA(mem4_5_odata));
  assign ODATA = mem4_1_odata | mem4_2_odata | mem4_3_odata | mem4_4_odata | mem4_5_odata;  // OR_Gate or_1, 4 bits wide
endmodule

module MEM4 (
  input  [3:0] IDATA,
  input  RESET,
  input  W,
  input  CLK,
  output [3:0] ODATA
);

  wire and_1_out, and_2_out, and_3_out, and_4_out, and_5_out, not_1_out, not_2_out, not_3_out, not_4_out,
       not_5_out, not_6_out, not_7_out, not_8_out, or_1_out, rstriger_1_q, rstriger_2_q, rstriger_3_q,
       rstriger_4_q;

  not not_1 (not_1_out, RESET);
  not not_2 (not_2_out, RESET);
  not not_3 (not_3_out, RESET);
  not not_4 (not_4_out, RESET);
  and and_1 (and_1_out, W, CLK);
  not not_5 (not_5_out, and_2_out);
  and and_2 (and_2_out, IDATA[0], not_1_out);
  not not_6 (not_6_out, and_3_out);
  and and_3 (and_3_out, IDATA[1], not_2_out);
  not not_7 (not_7_out, and_4_out);
  and and_4 (and_4_out, IDATA[2], not_3_out);
  not not_8 (not_8_out, and_5_out);
  and and_5 (and_5_out, IDATA[3], not_4_out);
  or or_1 (or_1_out, RESET, and_1_out);
  RSTRIGER rstriger_1 (.R(not_5_out), .C(or_1_out), .S(and_2_out), .Q(rstriger_1_q));  // open: nQ
  RSTRIGER rstriger_2 (.R(not_6_out), .C(or_1_out), .S(and_3_out), .Q(rstriger_2_q));  // open: nQ
  RSTRIGER rstriger_3 (.R(not_7_out), .C(or_1_out), .S(and_4_out), .Q(rstriger_3_q));  // open: nQ
  RSTRIGER rstriger_4 (.R(not_8_out), .C(or_1_out), .S(and_5_out), .Q(rstriger_4_q));  // open: nQ
  and and_6 (ODATA[0], rstriger_1_q, CLK);
  and and_7 (ODATA[1], rstriger_2_q, CLK);
  and and_8 (ODATA[2], rstriger_3_q, CLK);
  and and_9 (ODATA[3], rstriger_4_q, CLK);
endmodule

module THREE_TO_FIVE (
  input  [2:0] INDEX,
  output M0,
  output M1,
  output M2,
  output M3,
  output M4
);

  wire not_1_out, not_2_out, not_3_out, not_4_out, not_5_out, not_6_out, not_7_out, not_8_out, not_9_out,
       not_10_out;

  not not_1 (not_1_out, INDEX[0]);
  not not_2 (not_2_out, INDEX[1]);
  and and_1 (M0, not_1_out, not_2_out, not_3_out);
  not not_3 (not_3_out, INDEX[2]);
  not not_4 (not_4_out, INDEX[1]);
  and and_2 (M1, INDEX[0], not_4_out, not_5_out);
  not not_5 (not_5_out, INDEX[2]);
  not not_6 (not_6_out, INDEX[0]);
  and and_3 (M2, not_6_out, INDEX[1], not_7_out);
  not not_7 (not_7_out, INDEX[2]);
  and and_4 (M3, INDEX[0], INDEX[1], not_8_out);
  not not_8 (not_8_out, INDEX[2]);
  not not_9 (not_9_out, INDEX[0]);
  not not_10 (not_10_out, INDEX[1]);
  and and_5 (M4, not_9_out, not_10_out, INDEX[2]);
endmodule

module TTRIGER (
  input  D,
  input  C,
  input  R,
  output Q,
  output nQ
);

  wire and_1_out, not_1_out, or_1_out, or_2_out, rstriger_1_nq, rstriger_1_q;

  or or_1 (or_1_out, ~D, R);  // OR_Gate
  or or_2 (or_2_out, C, R);
  and and_1 (and_1_out, ~R, D);  // AND_Gate
  RSTRIGER rstriger_1 (.R(or_1_out), .C(or_2_out), .S(and_1_out), .Q(rstriger_1_q), .nQ(rstriger_1_nq));
  not not_1 (not_1_out, or_2_out);
  RSTRIGER rstriger_2 (.R(rstriger_1_nq), .C(not_1_out), .S(rstriger_1_q), .Q(Q), .nQ(nQ));
endmodule

module RSTRIGER (
  input  R,
  input  C,
  input  S,
  output Q,
  output nQ
);

  wire and_1_out, and_2_out;

  and and_1 (and_1_out, R, C);
  and and_2 (and_2_out, C, S);
  nor nor_1 (Q, and_1_out, nQ);
  nor nor_2 (nQ, Q, and_2_out);
endmodule
